// Logisim project BCD_to_CC_Sev_seg_decoder.circ as structural Verilog: 7 circuits, main circuit main
module main (
  input  A,
  input  B,
  input  C,
  input  D
);

  wire disp_a_1_a, disp_b_1_b, disp_c_1_c, disp_d_1_d, disp_e_1_e, disp_g_1_g;

  disp_a disp_a_1 (.in_1(A), .B(B), .C(C), .D(D), .a(disp_a_1_a));
  disp_b disp_b_1 (.A(A), .in_2(B), .C(C), .D(D), .b(disp_b_1_b));
  disp_c disp_c_1 (.A(A), .B(B), .in_3(C), .D(D), .c(disp_c_1_c));
  disp_d disp_d_1 (.A(A), .B(B), .C(C), .in_4(D), .d(disp_d_1_d));
  disp_e disp_e_1 (.A(A), .B(B), .C(C), .D(D), .e(disp_e_1_e));
  disp_g disp_g_1 (.A(A), .B(B), .C(C), .D(D), .g(disp_g_1_g));
  _7_Segment_Display u_7_segment_display_1 (
    .g(disp_g_1_g), .a(disp_a_1_a), .b(disp_b_1_b), .e(disp_e_1_e), .d(disp_d_1_d), .c(disp_c_1_c));  // open: f, dp
endmodule

module disp_g (
  input  A,
  input  B,
  input  C,
  input  D,
  output g
);

  wire and_1_out, and_2_out, and_3_out, not_1_out, not_2_out, not_3_out;

  not not_1 (not_1_out, B);
  not not_2 (not_2_out, C);
  not not_3 (not_3_out, D);
  and and_1 (and_1_out, not_1_out, C);
  and and_2 (and_2_out, B, not_2_out);
  and and_3 (and_3_out, C, not_3_out);
  or or_1 (g, and_1_out, and_2_out, A, and_3_out);
endmodule

module disp_b (
  input  A,
  input  in_2,
  input  C,
  input  D,
  output b
);

  wire and_1_out, and_2_out, not_1_out, not_2_out, not_3_out;

  not not_1 (not_1_out, in_2);
  not not_2 (not_2_out, C);
  not not_3 (not_3_out, D);
  and and_1 (and_1_out, not_2_out, not_3_out);
  and and_2 (and_2_out, C, D);
  or or_1 (b, not_1_out, and_1_out, and_2_out);
endmodule

module disp_a (
  input  in_1,
  input  B,
  input  C,
  input  D,
  output a
);

  wire and_1_out, and_2_out, not_1_out, not_2_out;

  not not_1 (not_1_out, B);
  not not_2 (not_2_out, D);
  and and_1 (and_1_out, not_1_out, not_2_out);
  and and_2 (and_2_out, B, D);
  or or_1 (a, and_1_out, C, and_2_out, in_1);
endmodule

module disp_c (
  input  A,
  input  B,
  input  in_3,
  input  D,
  output c
);

  wire not_1_out;

  not not_1 (not_1_out, in_3);
  or or_1 (c, not_1_out, D, B);
endmodule

module disp_d (
  input  A,
  input  B,
  input  C,
  input  in_4,
  output d
);

  wire and_1_out, and_2_out, and_3_out, and_4_out, not_1_out, not_2_out, not_3_out;

  not not_1 (not_1_out, B);
  not not_2 (not_2_out, C);
  not not_3 (not_3_out, in_4);
  and and_1 (and_1_out, not_1_out, not_3_out);
  and and_2 (and_2_out, not_1_out, C);
  and and_3 (and_3_out, B, not_2_out, in_4);
  and and_4 (and_4_out, C, not_3_out);
  or or_1 (d, and_1_out, and_2_out, and_3_out, and_4_out, A);
endmodule

module disp_e (
  input  A,
  input  B,
  input  C,
  input  D,
  output e
);

  wire and_1_out, and_2_out, not_1_out, not_2_out;

  not not_1 (not_1_out, B);
  not not_2 (not_2_out, D);
  and and_1 (and_1_out, not_1_out, not_2_out);
  and and_2 (and_2_out, C, not_2_out);
  or or_1 (e, and_1_out, and_2_out);
endmodule
