// Logisim project Decoder_2_to_4.circ as structural Verilog: 1 circuit, main circuit main
module main (
  input  I0,
  input  I1,
  input  I2,
  input  I3,
  input  S1,
  input  S0,
  output out_7,
  output F
);

  wire and_1_out, and_2_out, and_3_out, and_4_out, and_5_out, and_6_out, and_7_out, and_8_out, and_9_out,
       and_10_out, and_11_out, and_12_out, decoder_1_out0, decoder_1_out1, decoder_1_out2, decoder_1_out3,
       not_1_out, not_2_out;

  not not_1 (not_1_out, S1);
  and and_1 (and_1_out, not_1_out, not_2_out);
  and and_2 (and_2_out, not_1_out, S0);
  and and_3 (and_3_out, S1, not_2_out);
  and and_4 (and_4_out, S1, S0);
  not not_2 (not_2_out, S0);
  and and_5 (and_5_out, I0, and_1_out);
  and and_6 (and_6_out, I1, and_2_out);
  and and_7 (and_7_out, I2, and_3_out);
  and and_8 (and_8_out, I3, and_4_out);
  or or_1 (F, and_5_out, and_6_out, and_7_out, and_8_out);
  Decoder #(.enable("false"), .select(2)) decoder_1 (
    .out0(decoder_1_out0), .out1(decoder_1_out1), .out2(decoder_1_out2), .out3(decoder_1_out3), .sel({S1, S0}));
  and and_9 (and_9_out, I0, decoder_1_out0);
  and and_10 (and_10_out, I1, decoder_1_out1);
  and and_11 (and_11_out, I2, decoder_1_out2);
  and and_12 (and_12_out, I3, decoder_1_out3);
  or or_2 (out_7, and_9_out, and_10_out, and_11_out, and_12_out);
endmodule
