// Logisim project Mux4x1.circ as structural Verilog: 1 circuit, main circuit main
module main (
  input  I0,
  input  I1,
  input  I2,
  input  I3,
  input  S1,
  input  S0,
  output F2,
  output TEST,
  output F,
  output TEST2,
  output F3
);

  wire and_1_out, and_2_out, and_3_out, and_4_out, multiplexer_2_out, multiplexer_4_out, not_1_out, not_2_out;

  not not_1 (not_1_out, S1);
  and and_1 (and_1_out, I0, not_1_out, not_2_out);
  and and_2 (and_2_out, I1, not_1_out, S0);
  and and_3 (and_3_out, I2, S1, not_2_out);
  and and_4 (and_4_out, I3, S1, S0);
  not not_2 (not_2_out, S0);
  Multiplexer #(.select(2)) multiplexer_1 (.in0(I0), .in1(I1), .in2(I2), .in3(I3), .out(F2), .sel({S1, S0}));
  or or_1 (F, and_1_out, and_2_out, and_3_out, and_4_out);
  Multiplexer multiplexer_2 (.in0(I0), .in1(I1), .out(multiplexer_2_out), .sel(S0));
  Multiplexer multiplexer_3 (.in0(multiplexer_2_out), .in1(multiplexer_4_out), .out(F3), .sel(S1));
  Multiplexer multiplexer_4 (.in0(I2), .in1(I3), .out(multiplexer_4_out), .sel(S0));
  xor xor_1 (TEST, F2, F);
  xor xor_2 (TEST2, F, F3);
endmodule
