// Logisim project Sequential Circuit Example Block.circ as structural Verilog: 3 circuits, main circuit main
module main (
);

  wire clock_1_out, ff_1_na, ff_1_nb, ff_1_nc;
  wire [2:0] ff_1_a;
  wire [5:0] bm_1_jc;

  Clock clock_1 (.out(clock_1_out));
  FF ff_1 (
    .JC(bm_1_jc[0]), .JB(bm_1_jc[1]), .JA(bm_1_jc[2]), .KC(bm_1_jc[3]), .KB(bm_1_jc[4]), .KA(bm_1_jc[5]),
    .CLK(clock_1_out), .C(ff_1_a[2]), .NC(ff_1_nc), .B(ff_1_a[1]), .NB(ff_1_nb), .A(ff_1_a[0]), .NA(ff_1_na));
  Hex_Digit_Display hex_digit_display_1 (.value({1'b0, ff_1_a}));  // open: dp
  BM bm_1 (
    .C(ff_1_a[2]), .NC(ff_1_nc), .B(ff_1_a[1]), .NB(ff_1_nb), .A(ff_1_a[0]), .NA(ff_1_na), .JC(bm_1_jc[0]),
    .JB(bm_1_jc[1]), .JA(bm_1_jc[2]), .KC(bm_1_jc[3]), .KB(bm_1_jc[4]), .KA(bm_1_jc[5]));
endmodule

module BM (
  input  C,
  input  NC,
  input  B,
  input  NB,
  input  A,
  input  NA,
  output JC,
  output JB,
  output JA,
  output KC,
  output KB,
  output KA
);

  and and_1 (JC, NA, NB);
  and and_2 (JB, NC, A);
  and and_3 (JA, B, C);

  assign KA = NC;
  assign KB = C;
  assign KC = 1'b1;
endmodule

module FF (
  input  JC,
  input  JB,
  input  JA,
  input  KC,
  input  KB,
  input  KA,
  input  CLK,
  output C,
  output NC,
  output B,
  output NB,
  output A,
  output NA
);

  J_K_Flip_Flop FF_C (.J(JC), .K(KC), .clk(CLK), .Q(C), .Qn(NC));  // open: preset, reset
  J_K_Flip_Flop FF_B (.J(JB), .K(KB), .clk(CLK), .Q(B), .Qn(NB));  // open: preset, reset
  J_K_Flip_Flop FF_A (.J(JA), .K(KA), .clk(CLK), .Q(A), .Qn(NA));  // open: preset, reset
endmodule
