// Logisim project Sequential Circuit Example.circ as structural Verilog: 1 circuit, main circuit main
module main (
);

  wire A_FF_qn, and_1_out, and_2_out, and_3_out, B_FF_qn, C_FF_qn, clock_1_out, or_1_out;
  wire [2:0] A_FF_q;

  Clock clock_1 (.out(clock_1_out));
  and and_1 (and_1_out, A_FF_qn, B_FF_qn, C_FF_qn);
  Hex_Digit_Display hex_digit_display_1 (.value({1'b0, A_FF_q}));  // open: dp
  S_R_Flip_Flop C_FF (
    .S(and_1_out), .R(A_FF_q[2]), .clk(clock_1_out), .Q(A_FF_q[2]), .Qn(C_FF_qn));  // open: reset, preset
  S_R_Flip_Flop B_FF (.S(A_FF_q[2]), .R(1'b0), .clk(clock_1_out), .Q(A_FF_q[1]), .Qn(B_FF_qn));  // open: reset, preset
  and and_2 (and_2_out, C_FF_qn, A_FF_qn);
  and and_3 (and_3_out, A_FF_q[0], B_FF_qn);
  S_R_Flip_Flop A_FF (
    .S(and_2_out), .R(or_1_out), .clk(clock_1_out), .Q(A_FF_q[0]), .Qn(A_FF_qn));  // open: reset, preset
  or or_1 (or_1_out, A_FF_q[2], and_3_out);
endmodule
